// Digital circuit Registro_PinIO.dig as structural Verilog
module Registro_PinIO (
  input  D3,
  input  En,
  input  Clock,
  input  C,
  input  Set,
  input  D2,
  input  D1,
  input  D0,
  input  D7,
  input  En_2,
  input  Clock_2,
  input  C_2,
  input  Set_2,
  input  D6,
  input  D5,
  input  D4,
  input  D11,
  input  En_3,
  input  Clock_3,
  input  C_3,
  input  Set_3,
  input  D10,
  input  D9,
  input  D8,
  output out_17,
  output out_18,
  output out_19,
  output out_20,
  output out_29,
  output out_30,
  output out_31,
  output out_32
);

  wire D0_t, D0E, D0S, D1_t, D1E, D1S, D2_t, D2E, D2S, D3_t, D3E, D3S, multiplexer_1_out, multiplexer_2_out,
       multiplexer_3_out, multiplexer_4_out, multiplexer_5_out, multiplexer_6_out, multiplexer_7_out,
       multiplexer_8_out, multiplexer_9_out, multiplexer_10_out, multiplexer_11_out, multiplexer_12_out;

  Multiplexer multiplexer_1 (.sel(En_2), .in_0(out_17), .in_1(D7), .out(multiplexer_1_out));
  D_FF_AS d_ff_as_1 (.Set(Set_2), .D(multiplexer_1_out), .C(Clock_2), .Clr(C_2), .Q(out_17));  // open: nQ
  assign D0E = D0_t ? 1'b1 : 1'bz;  // Driver driver_1
  assign D1E = D1_t ? 1'b1 : 1'bz;  // Driver driver_2
  assign D2E = D2_t ? 1'b1 : 1'bz;  // Driver driver_3
  assign D3E = D3_t ? 1'b1 : 1'bz;  // Driver driver_4
  Multiplexer multiplexer_2 (.sel(En_2), .in_0(out_18), .in_1(D6), .out(multiplexer_2_out));
  D_FF_AS d_ff_as_2 (.Set(Set_2), .D(multiplexer_2_out), .C(Clock_2), .Clr(C_2), .Q(out_18));  // open: nQ
  assign D0S = ~D0_t ? 1'b1 : 1'bz;  // DriverInvSel driverinvsel_1
  assign D1S = ~D1_t ? 1'b1 : 1'bz;  // DriverInvSel driverinvsel_2
  assign D2S = ~D2_t ? 1'b1 : 1'bz;  // DriverInvSel driverinvsel_3
  assign D3S = ~D3_t ? 1'b1 : 1'bz;  // DriverInvSel driverinvsel_4
  Multiplexer multiplexer_3 (.sel(En_2), .in_0(out_19), .in_1(D5), .out(multiplexer_3_out));
  D_FF_AS d_ff_as_3 (.Set(Set_2), .D(multiplexer_3_out), .C(Clock_2), .Clr(C_2), .Q(out_19));  // open: nQ
  Multiplexer multiplexer_4 (.sel(En_2), .in_0(out_20), .in_1(D4), .out(multiplexer_4_out));
  D_FF_AS d_ff_as_4 (.Set(Set_2), .D(multiplexer_4_out), .C(Clock_2), .Clr(C_2), .Q(out_20));  // open: nQ
  Multiplexer multiplexer_5 (.sel(En), .in_0(D3_t), .in_1(D3), .out(multiplexer_5_out));
  D_FF_AS d_ff_as_5 (.Set(Set), .D(multiplexer_5_out), .C(Clock), .Clr(C), .Q(D3_t));  // open: nQ
  Multiplexer multiplexer_6 (.sel(En_3), .in_0(out_29), .in_1(D11), .out(multiplexer_6_out));
  Multiplexer multiplexer_7 (.sel(En), .in_0(D2_t), .in_1(D2), .out(multiplexer_7_out));
  D_FF_AS d_ff_as_6 (.Set(Set), .D(multiplexer_7_out), .C(Clock), .Clr(C), .Q(D2_t));  // open: nQ
  D_FF_AS d_ff_as_7 (.Set(Set_3), .D(multiplexer_6_out), .C(Clock_3), .Clr(C_3), .Q(out_29));  // open: nQ
  Multiplexer multiplexer_8 (.sel(En_3), .in_0(out_30), .in_1(D10), .out(multiplexer_8_out));
  Multiplexer multiplexer_9 (.sel(En), .in_0(D1_t), .in_1(D1), .out(multiplexer_9_out));
  D_FF_AS d_ff_as_8 (.Set(Set), .D(multiplexer_9_out), .C(Clock), .Clr(C), .Q(D1_t));  // open: nQ
  D_FF_AS d_ff_as_9 (.Set(Set_3), .D(multiplexer_8_out), .C(Clock_3), .Clr(C_3), .Q(out_30));  // open: nQ
  Multiplexer multiplexer_10 (.sel(En), .in_0(D0_t), .in_1(D0), .out(multiplexer_10_out));
  Multiplexer multiplexer_11 (.sel(En_3), .in_0(out_31), .in_1(D9), .out(multiplexer_11_out));
  D_FF_AS d_ff_as_10 (.Set(Set), .D(multiplexer_10_out), .C(Clock), .Clr(C), .Q(D0_t));  // open: nQ
  D_FF_AS d_ff_as_11 (.Set(Set_3), .D(multiplexer_11_out), .C(Clock_3), .Clr(C_3), .Q(out_31));  // open: nQ
  Multiplexer multiplexer_12 (.sel(En_3), .in_0(out_32), .in_1(D8), .out(multiplexer_12_out));
  D_FF_AS d_ff_as_12 (.Set(Set_3), .D(multiplexer_12_out), .C(Clock_3), .Clr(C_3), .Q(out_32));  // open: nQ

  // Notes on the sheet:
  //   Registro de almacenamiento
  //   (Entrada)
  //   Registro de configuracion
  //   (Entrada/salida)
  //   Registro de control
  //   (Salida)
endmodule
